// Logisim project exercicio_08-03-2023.circ as structural Verilog: 1 circuit, main circuit main
module main (
  input  [3:0] entrada,
  input  _0___dado___1___inst,
  input  clock,
  input  reset,
  input  [3:0] entrada_0,
  input  [3:0] entrada_1,
  input  Chaveia_entre_entrada_0_e_1,
  input  \_0_para_não_enviar_a_saida_e_1_para_enviar_a_saida ,
  output [3:0] out_9,
  output [3:0] out_10
);

  wire and_1_out, and_2_out, and_3_out, not_1_out;
  wire [3:0] reg_0_q, reg_1_q, reg_inst_q;

  Register #(.width(4)) reg_inst (.D(entrada), .en(_0___dado___1___inst), .Q(reg_inst_q), .clk(clock), .clr(reset));
  and and_1 (and_1_out, ~reg_inst_q[1], ~_0___dado___1___inst);  // AND_Gate
  Multiplexer #(.width(4)) multiplexer_1 (
    .in0(entrada_0), .in1(entrada_1), .out(out_10), .sel(Chaveia_entre_entrada_0_e_1),
    .en(\_0_para_não_enviar_a_saida_e_1_para_enviar_a_saida ));
  and and_2 (and_2_out, ~reg_inst_q[0], and_1_out);  // AND_Gate
  and and_3 (and_3_out, reg_inst_q[0], and_1_out);
  not not_1 (not_1_out, reg_inst_q[0]);
  Register #(.width(4)) reg_0 (.D(entrada), .en(and_3_out), .Q(reg_0_q), .clk(clock), .clr(reset));
  Register #(.width(4)) reg_1 (.D(entrada), .en(and_2_out), .Q(reg_1_q), .clk(clock), .clr(reset));
  Multiplexer #(.width(4)) multiplexer_2 (
    .in0(reg_0_q), .in1(reg_1_q), .out(out_9), .sel(not_1_out), .en(reg_inst_q[1]));
endmodule
