// Logisim project exemplo.circ as structural Verilog: 1 circuit, main circuit main
module main (
  input  [3:0] in_1,
  input  Enable_0,
  input  select_0,
  input  Clock,
  input  enable_out,
  input  Clear,
  output [3:0] out_7
);

  wire not_1_out;
  wire [3:0] register_1_q, register_2_q;

  Register #(.width(4)) register_1 (.D(in_1), .en(Enable_0), .Q(register_1_q), .clk(Clock), .clr(Clear));
  not not_1 (not_1_out, Enable_0);
  Register #(.width(4)) register_2 (.D(in_1), .en(not_1_out), .Q(register_2_q), .clk(Clock), .clr(Clear));
  Multiplexer #(.width(4)) multiplexer_1 (
    .in0(register_1_q), .in1(register_2_q), .out(out_7), .sel(select_0), .en(enable_out));
endmodule
