// Logisim project exercicio avaliativo 01-03-2023.circ as structural Verilog: 1 circuit, main circuit main
module main (
  input  [3:0] entrada,
  input  _0___dado_1_intrucao___enable_dos_registradores,
  input  clock,
  input  reset,
  output [3:0] out_5
);

  wire and_1_out, and_2_out, not_1_out;
  wire [3:0] reg_inst_q;

  Register #(.width(4)) reg_inst (
    .D(entrada), .en(_0___dado_1_intrucao___enable_dos_registradores), .Q(reg_inst_q), .clk(clock),
    .clr(reset));
  not not_1 (not_1_out, _0___dado_1_intrucao___enable_dos_registradores);
  buf and_1 (and_1_out, _0___dado_1_intrucao___enable_dos_registradores);  // AND_Gate
  buf and_2 (and_2_out, not_1_out);  // AND_Gate
  Register #(.width(4)) reg_1 (.en(and_1_out), .clk(clock), .clr(reset));  // open: D, Q
  Register #(.width(4)) reg_0 (.en(and_2_out), .clk(clock), .clr(reset));  // open: D, Q
  Multiplexer #(.width(4)) multiplexer_1 (.out(out_5), .sel(reg_inst_q[3]), .en(reg_inst_q[2]));  // open: in0, in1
endmodule
