// Logisim project teste.circ as structural Verilog: 1 circuit, main circuit main
module main (
  input  [3:0] entrada_0,
  input  [3:0] entrada_1,
  input  Chaveia_entre_a_entrada_0_e_aentrada_1,
  input  enable_desable,
  input  [3:0] entrada_reg,
  input  enable,
  input  clock,
  input  reset,
  output [3:0] saida,
  output [3:0] saida_2
);

  Multiplexer #(.width(4)) multiplexer_1 (
    .in0(entrada_0), .in1(entrada_1), .out(saida), .sel(Chaveia_entre_a_entrada_0_e_aentrada_1),
    .en(enable_desable));
  Register #(.width(4)) registrador (.D(entrada_reg), .en(enable), .Q(saida_2), .clk(clock), .clr(reset));
endmodule
